# Fritzing sketch Untitled Sketch 2 (saved by Fritzing 0.9.3b)
circuit board: 8.46667cm x 5.64444cm
breadboards: 1

parts:
  R1 = Resistor [tolerance=±5% resistance=220 package=THT]
  R2 = Resistor [tolerance=±5% resistance=220 package=THT]
  R3 = Resistor [tolerance=±5% resistance=220 package=THT]
  R4 = Resistor [tolerance=±5% resistance=220 package=THT]
  R5 = Resistor [tolerance=±5% resistance=220 package=THT]
  R6 = Resistor [tolerance=±5% resistance=220 package=THT]
  S1 = Pushbutton [package="[THT]"]
  LED1 = LED - 5mm [color="Yellow (595nm)" package="5 mm [THT]"]
  LED2 = LED - 5mm [color="Red (633nm)" package="5 mm [THT]"]
  LED3 = LED - 5mm [color="Red (633nm)" package="5 mm [THT]"]
  LED4 = LED - 5mm [color="Green (555nm)" package="5 mm [THT]"]
  LED5 = LED - 5mm [color="Green (555nm)" package="5 mm [THT]"]
  Part1 = Arduino Uno (Rev3)

nets:
  N1: R1.Pin_0, LED3.anode
  N2: R1.Pin_1, Part1.D12/MISO
  N3: R2.Pin_0, LED1.anode
  N4: R2.Pin_1, Part1.D11_PWM/MOSI
  N5: R3.Pin_0, LED5.anode
  N6: R3.Pin_1, Part1.D10_PWM/SS
  N7: R4.Pin_0, LED2.anode
  N8: R4.Pin_1, Part1.D8
  N9: R5.Pin_0, LED4.anode
  N10: R5.Pin_1, Part1.D7
  N11: R6.Pin_0, Part1.GND
  N12: R6.Pin_1, S1.Pin_3, S1.Pin_4, Part1.D9_PWM
  N13: S1.Pin_1, S1.Pin_2, Part1.5V
  N14: LED1.cathode, LED2.cathode, LED3.cathode, LED4.cathode, LED5.cathode

// code stored in the sketch: traffic.ino
// PROJECT 3 Interactive Traffic Light
int carRed = 12;
 //configure traffic light
int carYellow = 11;
int carGreen = 10;
int button = 9;
 //pin of button
int pedRed = 8;
 //configure light for pedestrians
int pedGreen = 7;
int crossTime = 5000;
 //time for pedestrians to pass unsigned
long changeTime;
 //time that the button is pressed
void setup() {
//configure all LEDs as output
pinMode(carRed, OUTPUT);
pinMode(carYellow, OUTPUT);
pinMode(carGreen, OUTPUT);
pinMode(pedRed, OUTPUT);
pinMode(pedGreen, OUTPUT);
pinMode(button, INPUT);
 //configure button as input
digitalWrite(carGreen, HIGH); //initialize green traffic
light on
digitalWrite(pedRed, LOW); //initialize red pedestrian light off }
void loop() {
int state = digitalRead(button);
// test if the button is pressed and if 5 seconds have passed after it is pressed
lately.
if(state == HIGH && (millis() - changeTime)> 5000){
//carry out the function of changing LED
changeLights();
}
}
void changeLights() {
digitalWrite(carGreen, LOW);digitalWrite(carYellow, HIGH);delay(2000);
//green traffic light off
//yellow traffic light on
//wait for 2 secs
digitalWrite(carYellow, LOW);digitalWrite(carRed, HIGH);
delay(1000);
// yellow traffic light off
//red traffic light on
// wait for 1 sec for safety reason
digitalWrite(pedRed, LOW);
 //red pedestrian light off
digitalWrite(pedGreen, HIGH); //light pedestrian light on
delay(crossTime);
 // time for crossing street
//blink green pedestrian light to notify pedestrians to pass soon
for (int x=0; x<10; x++) {
digitalWrite(pedGreen, HIGH);
delay(250);
digitalWrite(pedGreen, LOW);
delay(250);
}
digitalWrite(pedRed, HIGH);
 //red pedestrian light on
delay(500);
digitalWrite(carRed, LOW);
digitalWrite(carYellow, HIGH);
delay(1000);
delay(1000);
digitalWrite(carYellow, LOW);
digitalWrite(carGreen, HIGH);
//red traffic light off
//yellow traffic light on
//yellow traffic light off
//green traffic light on
changeTime = millis()
 // record the duration since last
change
//back to the loop of main code
}
